# Fritzing sketch rpi_rgb_led (saved by Fritzing 0.9.1b)

parts:
  Power_RGB1 = Prolight RGB 3 Watt Star
  Raspberry_Pi1 = Raspberry Pi B+
  R4 = Resistor [tolerance=±5% resistance=220 package=THT]
  R6 = Resistor [tolerance=±5% resistance=220 package=THT]
  R7 = Resistor [tolerance=±5% resistance=220 package=THT]

nets:
  N1: Power_RGB1.B+, R7.Pin_1
  N2: Power_RGB1.G+, R4.Pin_1
  N3: Power_RGB1.R+, R6.Pin_1
  N4: Power_RGB1.R-, Power_RGB1.G-, Power_RGB1.B-, Raspberry_Pi1.GND
  N5: Raspberry_Pi1.GPIO6, R4.Pin_0
  N6: Raspberry_Pi1.GPIO13, R6.Pin_0
  N7: Raspberry_Pi1.GPIO12, R7.Pin_0
